# Fritzing sketch GPIO LED Circuit (saved by Fritzing 0.9.1b)
breadboards: 1

parts:
  Pi1 = Adafruit Pi Cobbler
  LED1 = LED - 5mm [color="Red (633nm)" package="5 mm [THT]"]
  R1 = Resistor [tolerance=±5% resistance=82 package=THT]

nets:
  N1: Pi1.GND, R1.Pin_0
  N2: Pi1.#18, LED1.anode
  N3: LED1.cathode, R1.Pin_1

custom parts:
  Adafruit Pi Cobbler: Adafruit Pi Cobbler GPIO Breakout for Raspberry Pi
