# Fritzing sketch HalfAdder (saved by Fritzing 0.9.1b)
breadboards: 1

parts:
  Pi1 = Adafruit Pi Cobbler
  IC1 = IC, DIP package, 14 pins [chip_label=7408]
  IC2 = IC, DIP package, 14 pins [chip_label=7486]

nets:
  N1: Pi1.5V0, IC1.pin14, IC2.pin14
  N2: Pi1.GND, IC1.pin7, IC2.pin7
  N3: Pi1.#17, IC1.pin2, IC2.pin2
  N4: Pi1.#22, IC1.pin1, IC2.pin1
  N5: Pi1.#23, IC2.pin3
  N6: Pi1.#24, IC1.pin3

custom parts:
  Adafruit Pi Cobbler: Adafruit Pi Cobbler GPIO Breakout for Raspberry Pi
